# Fritzing sketch circuito (saved by Fritzing 0.9.10b)
breadboards: 1

parts:
  Part1 = AF_mshield-v1.2_breadboard
  Part2 = Arduino Uno (Rev3)  # not connected
  S1 = Momentary Switch [package=ksa_sealed_tac_switch]
  S2 = Momentary Switch [package=ksa_sealed_tac_switch]
  S3 = Momentary Switch [package=ksa_sealed_tac_switch]
  S4 = Momentary Switch [package=ksa_sealed_tac_switch]
  S5 = Momentary Switch [package=ksa_sealed_tac_switch]
  M1 = gear-motor
  M2 = gear-motor
  J1 = Piezo Speaker
  J2 = Basic Servo

nets:
  N1: Part1.1, S1.1
  N2: Part1.2, S2.1
  N3: Part1.3, S4.1
  N4: Part1.4, S5.1
  N5: Part1.5, S3.1
  N6: Part1.6, J1.pin2
  GND: Part1.GND, S1.3, S2.3, S3.3, S4.3, S5.3, J1.pin1, J2.gnd
  N7: Part1.PWM1A, J2.pulse
  VCC: Part1.VCC, J2.vcc
  N8: Part1.P1, M1.pin_2
  N9: Part1.P2, M1.pin_1
  N10: Part1.P4, M2.pin_2
  N11: Part1.P5, M2.pin_1

notes:
  *Controlador de motor sobre el arduino
  *Buzzer representa conexión con FPGA
  *Gripper

custom parts:
  : motor Shield v1 Adafruit Adafruit Motor/Stepper/Servo Shield for Arduino kit [v1.2] : ID 81 : $19.50 : Adafruit Industries, Unique & fun DIY electronics and kits
